# Fritzing sketch ESP32_DNT22_DS18B20_Pool_Sensor (saved by Fritzing 0.9.10b)
breadboards: 1

parts:
  MH-ET_LIVE_ESP32_DEVKIT1 = MH-ET LIVE ESP32 DEVKIT 38 pins
  R1 = Resistor [tolerance=±5% power=0.25 resistance=220 package=THT]
  R2 = Resistor [tolerance=±5% power=0.25 resistance=220 package=THT]
  LED1 = LED - 5mm [color="Green (565nm)" current=0.030 package="5 mm [THT]"]
  LED2 = LED - 5mm [color="Red (633nm)" current=0.030 package="5 mm [THT]"]
  R3 = Resistor [tolerance=±5% power=0.25 resistance=4.7k package=THT]
  DHT1 = DHT22 Humidity and Temperature Sensor
  R4 = Resistor [tolerance=±5% power=0.25 resistance=10k package=THT]
  DS1 = DS18B20 1-Wire Temperature Sensor [part_number=DS18B20]

nets:
  VDD: MH-ET_LIVE_ESP32_DEVKIT1.3V3, R3.Pin_1, DHT1.VDD, R4.Pin_1, DS1.VDD
  N1: MH-ET_LIVE_ESP32_DEVKIT1.IO25, R3.Pin_0, DS1.DQ
  N2: MH-ET_LIVE_ESP32_DEVKIT1.IO23, R1.Pin_0
  N3: MH-ET_LIVE_ESP32_DEVKIT1.IO22, R2.Pin_1
  GND: MH-ET_LIVE_ESP32_DEVKIT1.GND#70, LED1.cathode, LED2.cathode, DHT1.GND, DS1.GND
  N4: MH-ET_LIVE_ESP32_DEVKIT1.IO4, DHT1.DATA, R4.Pin_0
  N5: R1.Pin_1, LED2.anode
  N6: R2.Pin_0, LED1.anode

custom parts:
  MH-ET LIVE ESP32 DEVKIT 38 pins: http://mh.nodebb.com/topic/2/mh-et-live-esp32-devkit
